# Fritzing sketch HW design (saved by Fritzing 0.9.4)
stripboards: 1

parts:
  WeMos_D1_Mini2 = WeMos D1 Mini
  Pololu_A1 = Pololu A4988 [package=SO16]
  MOTOR1 = Adafruit Gear-Reduced Stepper Motor (small)
  Part1 = VERTER 5V USB Buck-Boost
  C1 = Electrolytic Capacitor [capacitance=1000μF package="1010 [SMD, electrolytic]"]

nets:
  5V: WeMos_D1_Mini2.5V, WeMos_D1_Mini2.D1, Pololu_A1.STEP, Pololu_A1.VDD, Part1.VIN
  GND: WeMos_D1_Mini2.D2, WeMos_D1_Mini2.G, Pololu_A1.MS1, Pololu_A1.DIR, Pololu_A1.GND, Part1.GND, C1.-
  N1: Pololu_A1.ENABLE, Pololu_A1.VMOT, Part1.5.0V, C1.+
  N2: Pololu_A1.MS2, Pololu_A1.2B, MOTOR1.BLUE
  N3: Pololu_A1.MS3, Pololu_A1.2A, MOTOR1.YELLOW
  N4: Pololu_A1.RESET, Pololu_A1.SLEEP, Pololu_A1.1B, Pololu_A1.1A, MOTOR1.ORANGE, MOTOR1.PINK

custom parts:
  Adafruit Gear-Reduced Stepper Motor (small): Adafruit gear-reduction stepper motor (small)
  VERTER 5V USB Buck-Boost: VERTER can take battery voltages from 3-12VDC and output a nice 5V DC, which makes it a perfect universal power supply for your portable project! Where Verter really shines is when you have a battery or power range that can fluctuate a lot, or you don't know what you'll end up using.
